// Logisim project Project1.circ as structural Verilog: 4 circuits, main circuit main
module main (
  input  Z,
  input  Y,
  input  X,
  input  W,
  input  Five_V,
  output N,
  output E,
  output [3:0] out_8
);

  wire and_2_out, and_3_out, and_4_out, and_5_out, and_6_out, and_7_out, and_8_out, and_9_out, and_10_out,
       and_11_out, and_12_out, and_13_out, and_14_out, and_15_out, and_16_out, and_17_out, and_18_out,
       and_19_out, and_20_out, and_21_out, and_22_out, and_23_out, and_24_out, and_25_out, and_26_out,
       and_27_out, and_28_out, and_29_out, and_30_out, and_31_out, and_32_out, and_33_out, and_34_out,
       and_35_out, and_36_out, and_37_out, and_38_out, and_39_out, and_40_out, not_1_out, not_2_out,
       not_3_out, not_4_out, not_6_out, not_7_out, not_8_out, not_9_out, not_10_out, not_11_out, not_12_out,
       not_13_out, not_14_out, not_15_out, not_16_out, not_17_out, not_18_out, not_19_out, not_20_out,
       not_21_out, not_22_out, not_23_out, not_24_out, not_25_out, not_26_out, not_27_out, not_28_out,
       not_29_out, not_30_out, not_31_out, not_32_out, not_33_out, not_34_out, not_35_out, not_36_out,
       not_37_out, not_38_out, not_39_out, not_40_out, not_41_out, not_42_out, not_43_out, not_44_out,
       not_45_out, not_46_out, not_47_out, not_48_out, not_49_out, not_50_out, not_51_out, not_52_out,
       not_53_out, not_54_out, not_55_out, not_56_out, not_57_out, not_58_out, not_59_out, not_60_out,
       not_61_out, not_62_out, not_63_out, not_64_out, not_65_out, not_66_out, not_67_out, not_68_out,
       not_69_out, not_70_out, not_71_out, not_72_out, not_73_out, or_4_out, or_5_out, or_6_out, or_7_out,
       or_8_out, or_9_out, or_10_out, xnor_1_out, xnor_2_out, xnor_3_out;

  xnor xnor_1 (xnor_1_out, 1'b1, 1'b1);
  xnor xnor_2 (xnor_2_out, 1'b0, 1'b1);
  xnor xnor_3 (xnor_3_out, 1'b1, 1'b1);
  not not_1 (not_1_out, 1'b0);
  not not_2 (not_2_out, 1'b0);
  not not_3 (not_3_out, 1'b0);
  not not_4 (not_4_out, 1'b0);
  and and_1 (E, xnor_1_out, xnor_2_out, xnor_3_out);
  and and_2 (and_2_out, not_1_out, 1'b0, not_2_out);
  and and_3 (and_3_out, not_3_out, not_4_out);
  and and_4 (and_4_out, 1'b0, 1'b0, 1'b0);
  not not_5 (N, E);
  or or_1 (out_8[1], and_2_out, and_3_out, and_4_out);
  not not_6 (not_6_out, 1'b0);
  not not_7 (not_7_out, W);
  and and_5 (and_5_out, not_7_out, Y, Z);
  not not_8 (not_8_out, Five_V);
  not not_9 (not_9_out, W);
  not not_10 (not_10_out, X);
  and and_6 (and_6_out, not_8_out, not_9_out, not_10_out, not_11_out, not_12_out);
  not not_11 (not_11_out, Y);
  not not_12 (not_12_out, Z);
  not not_13 (not_13_out, W);
  and and_7 (and_7_out, Five_V, not_13_out, not_14_out, not_15_out);
  not not_14 (not_14_out, X);
  not not_15 (not_15_out, Y);
  and and_8 (and_8_out, Five_V, X, Y, Z);
  not not_16 (not_16_out, Five_V);
  not not_17 (not_17_out, W);
  and and_9 (and_9_out, not_16_out, not_17_out, not_18_out, not_19_out);
  not not_18 (not_18_out, X);
  not not_19 (not_19_out, Y);
  and and_10 (and_10_out, X, Y, Z);
  not not_20 (not_20_out, W);
  and and_11 (and_11_out, not_20_out, Y, Z);
  not not_21 (not_21_out, W);
  not not_22 (not_22_out, X);
  and and_12 (and_12_out, not_21_out, not_22_out, not_23_out);
  not not_23 (not_23_out, Y);
  and and_13 (and_13_out, X, Y, Z);
  not not_24 (not_24_out, W);
  and and_14 (and_14_out, Five_V, not_24_out, Y, Z);
  not not_25 (not_25_out, Five_V);
  not not_26 (not_26_out, W);
  and and_15 (and_15_out, not_25_out, not_26_out, Y, Z);
  not not_27 (not_27_out, Five_V);
  not not_28 (not_28_out, W);
  not not_29 (not_29_out, X);
  and and_16 (and_16_out, not_27_out, not_28_out, not_29_out, not_30_out, not_31_out);
  not not_30 (not_30_out, Y);
  not not_31 (not_31_out, Z);
  not not_32 (not_32_out, W);
  and and_17 (and_17_out, Five_V, not_32_out, not_33_out, not_34_out);
  not not_33 (not_33_out, X);
  not not_34 (not_34_out, Y);
  and and_18 (and_18_out, Five_V, X, Y, Z);
  not not_35 (not_35_out, Five_V);
  not not_36 (not_36_out, W);
  not not_37 (not_37_out, X);
  and and_19 (and_19_out, not_35_out, not_36_out, not_37_out, not_38_out, not_39_out);
  not not_38 (not_38_out, Y);
  not not_39 (not_39_out, Z);
  not not_40 (not_40_out, Five_V);
  not not_41 (not_41_out, W);
  not not_42 (not_42_out, X);
  and and_20 (and_20_out, not_40_out, not_41_out, not_42_out, Y, Z);
  not not_43 (not_43_out, W);
  not not_44 (not_44_out, X);
  and and_21 (and_21_out, Five_V, not_43_out, not_44_out, not_45_out, Z);
  not not_45 (not_45_out, Y);
  not not_46 (not_46_out, W);
  and and_22 (and_22_out, Five_V, not_46_out, X, Y, Z);
  not not_47 (not_47_out, Five_V);
  not not_48 (not_48_out, W);
  not not_49 (not_49_out, X);
  and and_23 (and_23_out, not_47_out, not_48_out, not_49_out, not_50_out, not_51_out);
  not not_50 (not_50_out, Y);
  not not_51 (not_51_out, Z);
  not not_52 (not_52_out, Five_V);
  and and_24 (and_24_out, not_52_out, W, X, Y, Z);
  not not_53 (not_53_out, W);
  and and_25 (and_25_out, Five_V, not_53_out, not_54_out, not_55_out);
  not not_54 (not_54_out, X);
  not not_55 (not_55_out, Y);
  and and_26 (and_26_out, Five_V, X, Y, Z);
  not not_56 (not_56_out, Five_V);
  not not_57 (not_57_out, W);
  and and_27 (and_27_out, not_56_out, not_57_out, Y, Z);
  not not_58 (not_58_out, Five_V);
  and and_28 (and_28_out, not_58_out, X, Y, Z);
  not not_59 (not_59_out, W);
  and and_29 (and_29_out, Five_V, not_59_out, not_60_out, not_61_out);
  not not_60 (not_60_out, X);
  not not_61 (not_61_out, Y);
  and and_30 (and_30_out, Five_V, X, Y, Z);
  and and_31 (and_31_out, 1'b0, 1'b0);
  and and_32 (and_32_out, 1'b0, not_6_out);
  and and_33 (and_33_out, 1'b0, not_62_out);
  not not_62 (not_62_out, 1'b0);
  and and_34 (and_34_out, 1'b0, not_63_out);
  not not_63 (not_63_out, 1'b0);
  not not_64 (not_64_out, 1'b0);
  and and_35 (and_35_out, not_64_out, 1'b0, not_65_out);
  not not_65 (not_65_out, 1'b0);
  not not_66 (not_66_out, 1'b0);
  and and_36 (and_36_out, not_66_out, 1'b0, not_67_out, not_68_out);
  not not_67 (not_67_out, 1'b0);
  not not_68 (not_68_out, 1'b0);
  or or_2 (out_8[0], and_31_out, and_32_out);
  or or_3 (out_8[2], and_33_out, and_34_out, and_35_out, and_36_out);
  or or_4 (or_4_out, and_5_out, and_6_out, and_7_out, and_8_out);
  or or_5 (or_5_out, and_9_out, and_10_out, and_11_out);
  or or_6 (or_6_out, and_12_out, and_13_out, and_14_out);
  or or_7 (or_7_out, and_15_out, and_16_out, and_17_out, and_18_out);
  or or_8 (or_8_out, and_19_out, and_20_out, and_21_out, and_22_out);
  or or_9 (or_9_out, and_23_out, and_24_out, and_25_out, and_26_out);
  or or_10 (or_10_out, and_27_out, and_28_out, and_29_out, and_30_out);
  and and_37 (and_37_out, 1'b0, not_69_out);
  not not_69 (not_69_out, 1'b0);
  and and_38 (and_38_out, 1'b0, 1'b0, not_70_out);
  not not_70 (not_70_out, 1'b0);
  and and_39 (and_39_out, 1'b0, 1'b0, not_71_out);
  not not_71 (not_71_out, 1'b0);
  not not_72 (not_72_out, 1'b0);
  and and_40 (and_40_out, 1'b0, not_72_out, not_73_out);
  not not_73 (not_73_out, 1'b0);
  or or_11 (out_8[3], and_37_out, and_38_out, and_39_out, and_40_out);
  _7_Segment_Display u_7_segment_display_1 (
    .g(or_10_out), .f(or_9_out), .a(or_4_out), .b(or_5_out), .e(or_8_out), .d(or_7_out), .c(or_6_out));  // open: dp
endmodule

module Compare (
  input  X0,
  input  X1,
  input  X2,
  input  Y0,
  input  Y1,
  input  Y2,
  output N,
  output E
);
endmodule

module Gray (
  input  B0,
  input  B1,
  input  B2,
  input  B3,
  output G0,
  output G1,
  output G2,
  output G3
);
endmodule

module FiveSeven (
  input  V,
  input  W,
  input  X,
  input  Y,
  input  Z,
  output A,
  output B,
  output C,
  output D,
  output E,
  output F,
  output G
);
endmodule
