// Logisim project Project2.circ as structural Verilog: 4 circuits, main circuit main
module main (
);

  wire and_1_out, and_2_out, B0, B1, B2, B3, B4, B5, B6, B7, B8, B9, BL, BU, C0, C1, C2, CLK, L1_l, L1_u,
       or_8_out, P1_v, R0, R1, R3, R4, Valid;
  wire [2:0] counter_1_q;
  wire [3:0] IB1_c0, P1_b0, register_3_q, register_4_q, register_5_q;

  Button n1 (.out(B1));
  Button n4 (.out(B4));
  Button n7 (.out(B7));
  Button L (.out(BL));
  Button n3 (.out(B3));
  Button n2 (.out(B2));
  Button n6 (.out(B6));
  Button n5 (.out(B5));
  Button n9 (.out(B9));
  Button n8 (.out(B8));
  Button U (.out(BU));
  Button n0 (.out(B0));
  or or_1 (R0, B3, B2, B1);
  or or_2 (R1, B6, B5, B4);
  or or_3 (R3, B9, B8, B7);
  or or_4 (R4, BU, B0, BL);
  or or_5 (C0, B1, B4, B7, BL);
  or or_6 (C1, B2, B5, B8, B0);
  or or_7 (C2, B3, B6, B9, BU);
  Clock clock_1 (.out(CLK));
  nand nand_1 (Valid, IB1_c0[0], IB1_c0[1], IB1_c0[2], IB1_c0[3]);
  // Probe on P1_b0
  Panel P1 (
    .R0(R0), .R1(R1), .R2(R3), .R3(R4), .C0(C0), .C1(C1), .C2(C2), .B0(P1_b0[0]), .B1(P1_b0[1]),
    .B2(P1_b0[2]), .B3(P1_b0[3]), .V(P1_v));
  LED Press (.in(P1_v));
  // Probe on IB1_c0
  InputBuffer IB1 (
    .B0(P1_b0[0]), .B1(P1_b0[1]), .B2(P1_b0[2]), .B3(P1_b0[3]), .V(P1_v), .CLK(CLK), .C0(IB1_c0[0]),
    .C1(IB1_c0[1]), .C2(IB1_c0[2]), .C3(IB1_c0[3]));
  Register #(.width(4)) register_1 (.D(register_3_q), .en(Valid), .clk(CLK));  // open: Q, clr
  Lock L1 (.C0(IB1_c0[0]), .C1(IB1_c0[1]), .C2(IB1_c0[2]), .C3(IB1_c0[3]), .CLK(CLK), .L(L1_l), .U(L1_u));
  Counter #(.max('h7), .width(3)) counter_1 (
    .count(or_8_out), .Q(counter_1_q), .up(L1_u), .clk(CLK));  // open: load, D, carry, clr
  or or_8 (or_8_out, L1_l, L1_u);
  Register #(.width(4)) register_2 (.D(register_3_q), .en(Valid), .clk(CLK));  // open: Q, clr
  LED Unlocked (.in(and_1_out));
  and and_1 (and_1_out, ~counter_1_q[0], ~counter_1_q[1], ~counter_1_q[2]);  // AND_Gate
  Register #(.width(4)) register_3 (.D(register_4_q), .en(Valid), .clk(CLK), .Q(register_3_q));  // open: clr
  LED Locked (.in(and_2_out));
  and and_2 (and_2_out, ~counter_1_q[0], ~counter_1_q[1], counter_1_q[2]);  // AND_Gate
  Register #(.width(4)) register_4 (.D(register_5_q), .en(Valid), .clk(CLK), .Q(register_4_q));  // open: clr
  Register #(.width(4)) register_5 (.D(IB1_c0), .en(Valid), .clk(CLK), .Q(register_5_q));  // open: clr
endmodule

module Panel (
  input  R0,
  input  R1,
  input  R2,
  input  R3,
  input  C0,
  input  C1,
  input  C2,
  output B0,
  output B1,
  output B2,
  output B3,
  output V
);

  wire A, ACBD, and_1_out, and_5_out, and_6_out, and_7_out, and_8_out, and_9_out, and_10_out, and_11_out,
       and_12_out, and_14_out, and_15_out, and_16_out, and_17_out, and_18_out, and_19_out, and_20_out,
       and_21_out, B, C, D, NO_PRESS, not_3_out, not_4_out, not_5_out, not_6_out, not_9_out, not_10_out,
       not_11_out, not_12_out, not_13_out, not_14_out, not_15_out, not_17_out, NOTA, NOTB, NOTC, NOTD,
       or_1_out, or_4_out, or_5_out, or_8_out, or_9_out;

  and and_1 (and_1_out, A, NOTD);
  or or_1 (or_1_out, B, C);
  or or_2 (A, R3, R2);
  not not_1 (NOTA, A);
  or or_3 (B, R3, R1);
  not not_2 (NOTB, B);
  not not_3 (not_3_out, C1);
  not not_4 (not_4_out, C0);
  not not_5 (not_5_out, C2);
  not not_6 (not_6_out, C0);
  and and_2 (ACBD, and_1_out, or_1_out);
  and and_3 (C, C2, not_3_out, not_4_out);
  not not_7 (NOTC, C);
  and and_4 (D, C1, not_5_out, not_6_out);
  not not_8 (NOTD, D);
  not not_9 (not_9_out, R3);
  not not_10 (not_10_out, R2);
  not not_11 (not_11_out, R1);
  not not_12 (not_12_out, R0);
  not not_13 (not_13_out, C2);
  not not_14 (not_14_out, C1);
  not not_15 (not_15_out, C0);
  and and_5 (and_5_out, NOTA, C);
  and and_6 (and_6_out, A, B);
  and and_7 (and_7_out, NOTA, D);
  and and_8 (and_8_out, A, NOTD);
  and and_9 (and_9_out, not_9_out, not_10_out, not_11_out, not_12_out);
  and and_10 (and_10_out, not_13_out, not_14_out, not_15_out);
  and and_11 (and_11_out, A, NOTB, NOTC, D);
  or or_4 (or_4_out, and_5_out, and_6_out);
  and and_12 (and_12_out, NOTB, NOTC);
  or or_5 (or_5_out, and_7_out, and_8_out);
  and and_13 (NO_PRESS, and_9_out, and_10_out);
  or or_6 (B3, ACBD, and_11_out);
  and and_14 (and_14_out, NOTD, or_4_out);
  and and_15 (and_15_out, and_12_out, or_5_out);
  not not_16 (V, NO_PRESS);
  or or_7 (B1, and_14_out, and_15_out);
  and and_16 (and_16_out, NOTA, B);
  or or_8 (or_8_out, NOTC, NOTD);
  and and_17 (and_17_out, A, NOTB, NOTC, NOTD);
  and and_18 (and_18_out, NOTB, NOTD);
  and and_19 (and_19_out, A, C, NOTD);
  and and_20 (and_20_out, and_16_out, or_8_out);
  and and_21 (and_21_out, NOTA, B, NOTC, D);
  or or_9 (or_9_out, and_18_out, and_19_out, and_21_out);
  or or_10 (B2, and_20_out, and_17_out);
  not not_17 (not_17_out, NO_PRESS);
  Multiplexer multiplexer_1 (.in0(1'b0), .in1(or_9_out), .out(B0), .sel(not_17_out));

  // Other names for the same wires on the sheet: PRESS = V
endmodule

module InputBuffer (
  input  B0,
  input  B1,
  input  B2,
  input  B3,
  input  V,
  input  CLK,
  output C0,
  output C1,
  output C2,
  output C3
);

  wire and_1_out, and_2_out, and_3_out, NOT_S0, NOT_S1, S0, S1;
  wire [3:0] register_1_q;

  and and_1 (and_1_out, NOT_S1, S0);
  buf and_2 (and_2_out, V);  // AND_Gate
  Register #(.width(4)) register_1 (.D({B3, B2, B1, B0}), .en(V), .clk(CLK), .Q(register_1_q));  // open: clr
  D_Flip_Flop d_ff_1 (.D(and_1_out), .clk(CLK), .Q(S1), .Qn(NOT_S1));  // open: preset, reset
  D_Flip_Flop d_ff_2 (.D(and_2_out), .clk(CLK), .Q(S0), .Qn(NOT_S0));  // open: preset, reset
  Multiplexer #(.width(4)) multiplexer_1 (.in0(4'b1111), .in1(register_1_q), .out({C3, C2, C1, C0}), .sel(and_3_out));
  and and_3 (and_3_out, NOT_S1, S0);
endmodule

module Lock (
  input  C0,
  input  C1,
  input  CLK,
  input  C2,
  input  C3,
  output L,
  output U
);

  wire and_2_out, and_3_out, and_6_out, and_7_out, and_8_out, and_9_out, and_10_out, and_11_out, and_12_out,
       and_13_out, and_14_out, and_16_out, and_17_out, and_18_out, and_19_out, and_20_out, and_21_out,
       and_22_out, and_23_out, and_24_out, and_25_out, and_26_out, and_27_out, and_28_out, and_29_out,
       and_30_out, and_31_out, and_32_out, and_33_out, and_34_out, and_35_out, and_36_out, and_37_out,
       and_38_out, and_39_out, and_40_out, and_41_out, and_42_out, and_43_out, and_44_out, and_45_out,
       and_46_out, and_47_out, and_48_out, and_49_out, and_51_out, and_52_out, and_53_out, and_54_out,
       and_55_out, and_56_out, and_57_out, and_58_out, and_59_out, and_60_out, and_61_out, and_62_out,
       and_63_out, and_64_out, and_65_out, and_66_out, and_68_out, and_69_out, and_70_out, and_71_out,
       and_72_out, and_73_out, and_74_out, and_75_out, and_76_out, and_77_out, and_78_out, and_79_out,
       and_80_out, and_81_out, and_84_out, and_85_out, and_88_out, and_89_out, and_90_out, and_91_out,
       and_92_out, and_93_out, CMS, DIGIT, INVALID, LLS0, LLS1, LLS2, LOCKED, LOCKING, LPRESS, LS0, LS1,
       MAINS0, MAINS1, MAINS2, not_5_out, not_7_out, NOTC0, NOTC1, NOTC2, NOTC3, NOTCMS, NOTLLS0, NOTLLS1,
       NOTLLS2, NOTLS0, NOTLS1, NOTMAINS0, NOTMAINS1, NOTMAINS2, NOTS0, NOTS1, NOTS2, NOTULS0, NOTULS1,
       or_1_out, or_2_out, or_3_out, or_4_out, or_5_out, or_6_out, or_7_out, or_8_out, or_9_out, or_10_out,
       or_11_out, or_13_out, or_14_out, or_15_out, or_16_out, or_17_out, or_18_out, or_19_out, or_20_out,
       or_21_out, or_22_out, or_23_out, S0, S1, S2, ULS0, ULS1, undriven, undriven_2, UNLOCKED, UNLOCKING,
       UPRESS, VALID;
  wire [3:0] register_1_q, register_2_q, register_3_q;

  not not_1 (NOTC1, C1);
  not not_2 (NOTC2, C2);
  not not_3 (NOTC3, C3);
  not not_4 (NOTC0, C0);
  and and_1 (INVALID, C3, C2, C1, C0);
  and and_2 (and_2_out, NOTMAINS2, CMS);
  and and_3 (and_3_out, MAINS2, NOTCMS);
  and and_4 (UPRESS, C3, NOTC2, C1, C0);
  and and_5 (LPRESS, C3, NOTC2, C1, NOTC0);
  and and_6 (and_6_out, C3, NOTC2, C1, C0);
  not not_5 (not_5_out, and_6_out);
  not not_6 (VALID, INVALID);
  and and_7 (and_7_out, NOTLLS2, LLS1, LLS0);
  and and_8 (and_8_out, LLS2, NOTLLS1, NOTLLS0);
  and and_9 (and_9_out, NOTLLS2, NOTLLS1, NOTLLS0);
  and and_10 (and_10_out, NOTLLS2, NOTLLS1, LLS0);
  and and_11 (and_11_out, NOTLLS2, LLS1, LLS0);
  and and_12 (and_12_out, NOTLLS2, NOTLLS1, LLS0);
  and and_13 (and_13_out, LLS2, NOTLLS1, NOTLLS0);
  or or_1 (or_1_out, and_2_out, and_3_out);
  and and_14 (and_14_out, MAINS2, NOTMAINS1, NOTMAINS0);
  not not_7 (not_7_out, LPRESS);
  and and_15 (DIGIT, not_7_out, not_5_out, VALID);
  and and_16 (and_16_out, NOTS2, NOTS1, S0);
  and and_17 (and_17_out, NOTS2, S1, NOTS0);
  and and_18 (and_18_out, DIGIT, 1'b1);
  or or_2 (or_2_out, and_7_out, and_8_out);
  and and_19 (and_19_out, LLS2, NOTLLS1, NOTLLS0);
  and and_20 (and_20_out, DIGIT, 1'b1);
  and and_21 (and_21_out, NOTLLS2, NOTLLS1, LLS0);
  and and_22 (and_22_out, NOTLLS2, LLS1, LLS0);
  and and_23 (and_23_out, NOTMAINS1, MAINS0);
  and and_24 (and_24_out, and_18_out, or_2_out);
  or or_3 (or_3_out, and_9_out, and_10_out, and_11_out, and_19_out);
  or or_4 (or_4_out, and_12_out, and_13_out);
  or or_5 (or_5_out, and_21_out, and_22_out);
  and and_25 (and_25_out, S2, NOTS1, S0);
  and and_26 (and_26_out, and_23_out, or_1_out);
  or or_6 (or_6_out, and_16_out, and_17_out);
  and and_27 (and_27_out, LLS2, NOTLLS1, NOTLLS0, INVALID);
  and and_28 (and_28_out, UPRESS, or_3_out);
  and and_29 (and_29_out, and_20_out, or_4_out);
  and and_30 (and_30_out, INVALID, or_5_out);
  D_Flip_Flop d_ff_1 (.D(undriven), .clk(and_25_out), .reset(and_31_out));  // open: Q, Qn, preset
  and and_31 (and_31_out, NOTS2, S1, NOTS0);
  or or_7 (or_7_out, and_26_out, and_14_out);
  and and_32 (and_32_out, DIGIT, or_6_out);
  and and_33 (and_33_out, NOTS2, S1, INVALID);
  or or_8 (or_8_out, and_24_out, and_27_out);
  D_Flip_Flop d_ff_2 (.D(or_7_out), .clk(CLK), .Q(MAINS2), .Qn(NOTMAINS2));  // open: preset, reset
  and and_34 (and_34_out, S2, NOTS1, NOTS0);
  and and_35 (and_35_out, NOTS2, S1, S0);
  and and_36 (and_36_out, LOCKED, or_8_out);
  and and_37 (and_37_out, NOTS2, NOTS1, S0, LPRESS, 1'b0);
  and and_38 (and_38_out, DIGIT, and_35_out);
  and and_39 (and_39_out, S2, NOTS1, NOTS0, INVALID);
  or or_9 (or_9_out, and_32_out, and_33_out);
  D_Flip_Flop d_ff_3 (.D(and_36_out), .clk(CLK), .Q(LLS2), .Qn(NOTLLS2));  // open: preset, reset
  or or_10 (or_10_out, and_28_out, and_29_out, and_30_out);
  or or_11 (or_11_out, and_37_out, and_34_out, and_38_out, and_39_out);
  and and_40 (and_40_out, or_10_out, LOCKED);
  and and_41 (and_41_out, S2, NOTS1, S0);
  and and_42 (and_42_out, LS1, LS0);
  and and_43 (and_43_out, LLS2, NOTLLS1, LLS0);
  and and_44 (and_44_out, ULS1, ULS0);
  D_Flip_Flop d_ff_4 (.D(1'b0), .clk(CLK), .Q(MAINS1), .Qn(NOTMAINS1));  // open: preset, reset
  and and_45 (and_45_out, or_9_out, UNLOCKED);
  D_Flip_Flop d_ff_5 (.D(and_40_out), .clk(CLK), .Q(LLS0), .Qn(NOTLLS0));  // open: preset, reset
  or or_12 (CMS, and_41_out, and_42_out, and_43_out, and_44_out);
  not not_8 (NOTCMS, CMS);
  D_Flip_Flop d_ff_6 (.D(and_45_out), .clk(CLK), .Q(S1), .Qn(NOTS1));  // open: preset, reset
  and and_46 (and_46_out, or_11_out, UNLOCKED);
  D_Flip_Flop d_ff_7 (.D(and_46_out), .clk(CLK), .Q(S2), .Qn(NOTS2), .reset(undriven_2));  // open: preset
  and and_47 (and_47_out, NOTMAINS0, CMS);
  and and_48 (and_48_out, DIGIT, and_49_out);
  and and_49 (and_49_out, NOTLLS2, NOTLLS1, LLS0);
  and and_50 (L, NOTMAINS2, NOTMAINS1, MAINS0);
  and and_51 (and_51_out, NOTMAINS2, NOTMAINS1);
  and and_52 (and_52_out, MAINS0, NOTCMS);
  and and_53 (and_53_out, MAINS2, NOTMAINS1);
  and and_54 (and_54_out, NOTMAINS0, CMS);
  and and_55 (and_55_out, MAINS0, NOTCMS);
  and and_56 (and_56_out, NOTLLS2, LLS1, LLS0, C3, C1, C0);
  or or_13 (or_13_out, and_47_out, and_52_out);
  or or_14 (or_14_out, and_54_out, and_55_out);
  and and_57 (and_57_out, NOTS2, NOTS1, NOTS0);
  and and_58 (and_58_out, NOTS2, S1, S0);
  or or_15 (or_15_out, and_48_out, and_56_out);
  and and_59 (and_59_out, and_51_out, or_13_out);
  and and_60 (and_60_out, and_53_out, or_14_out);
  and and_61 (and_61_out, NOTS2, NOTS1, S0, 1'b0);
  and and_62 (and_62_out, NOTS2, S1, NOTS0);
  and and_63 (and_63_out, NOTS2, NOTS1, S0);
  and and_64 (and_64_out, S2, NOTS1, NOTS0);
  and and_65 (and_65_out, or_15_out, LOCKED);
  or or_16 (or_16_out, and_59_out, and_60_out);
  and and_66 (and_66_out, NOTS2, S1, S0);
  D_Flip_Flop d_ff_8 (.D(and_65_out), .clk(CLK), .Q(LLS1), .Qn(NOTLLS1));  // open: preset, reset
  and and_67 (U, MAINS2, NOTMAINS1, MAINS0);
  D_Flip_Flop d_ff_9 (.D(or_16_out), .clk(CLK), .Q(MAINS0), .Qn(NOTMAINS0));  // open: preset, reset
  or or_17 (or_17_out, and_57_out, and_61_out, and_62_out, and_58_out);
  and and_68 (and_68_out, NOTS2, S1, NOTS0);
  and and_69 (and_69_out, S2, NOTS1, NOTS0);
  or or_18 (or_18_out, and_63_out, and_66_out, and_64_out);
  Register #(.width(4)) register_1 (.D({C3, C2, C1, C0}), .en(and_70_out), .clk(CLK), .Q(register_1_q));  // open: clr
  and and_70 (and_70_out, NOTS2, NOTS1, S0);
  and and_71 (and_71_out, LPRESS, or_17_out);
  and and_72 (and_72_out, and_68_out, DIGIT);
  and and_73 (and_73_out, NOTS2, S1, INVALID);
  and and_74 (and_74_out, INVALID, or_18_out);
  or or_19 (or_19_out, and_71_out, and_72_out, and_69_out, and_73_out, and_74_out);
  and and_75 (and_75_out, or_19_out, UNLOCKED);
  Register #(.width(4)) register_2 (.D({C3, C2, C1, C0}), .en(and_76_out), .clk(CLK), .Q(register_2_q));  // open: clr
  and and_76 (and_76_out, NOTS2, S1, S0);
  D_Flip_Flop d_ff_10 (.D(and_75_out), .clk(CLK), .Q(S0), .Qn(NOTS0));  // open: preset, reset
  Register #(.width(4)) register_3 (.D({C3, C2, C1, C0}), .en(and_77_out), .clk(CLK), .Q(register_3_q));  // open: clr
  and and_77 (and_77_out, S2, NOTS1, S0);
  and and_78 (and_78_out, NOTLS1, LS0);
  and and_79 (and_79_out, LS1, NOTLS0);
  and and_80 (and_80_out, NOTULS1, ULS0);
  and and_81 (and_81_out, ULS1, NOTULS0);
  or or_20 (or_20_out, and_78_out, and_79_out);
  or or_21 (or_21_out, and_80_out, and_81_out);
  and and_82 (UNLOCKED, NOTMAINS2, NOTMAINS1, NOTMAINS0);
  and and_83 (LOCKED, MAINS2, NOTMAINS1, NOTMAINS0);
  and and_84 (and_84_out, or_20_out, LOCKING);
  D_Flip_Flop d_ff_11 (.D(and_84_out), .clk(CLK), .Q(LS1), .Qn(NOTLS1));  // open: preset, reset
  D_Flip_Flop d_ff_12 (.D(and_85_out), .clk(CLK), .Q(ULS1), .Qn(NOTULS1));  // open: preset, reset
  and and_85 (and_85_out, or_21_out, UNLOCKING);
  and and_86 (LOCKING, NOTMAINS2, NOTMAINS1, MAINS0);
  and and_87 (UNLOCKING, MAINS2, NOTMAINS1, MAINS0);
  and and_88 (and_88_out, NOTLS1, NOTLS0);
  and and_89 (and_89_out, LS1, NOTLS0);
  and and_90 (and_90_out, NOTULS1, NOTULS0);
  and and_91 (and_91_out, ULS1, NOTULS0);
  or or_22 (or_22_out, and_88_out, and_89_out);
  or or_23 (or_23_out, and_90_out, and_91_out);
  and and_92 (and_92_out, or_22_out, LOCKING);
  and and_93 (and_93_out, or_23_out, UNLOCKING);
  D_Flip_Flop d_ff_13 (.D(and_92_out), .clk(CLK), .Q(LS0), .Qn(NOTLS0));  // open: preset, reset
  D_Flip_Flop d_ff_14 (.D(and_93_out), .clk(CLK), .Q(ULS0), .Qn(NOTULS0));  // open: preset, reset
endmodule
